# Fritzing sketch mAteo (saved by Fritzing 0.9.2b)
breadboards: 1

parts:
  S1 = Momentary Switch [package=ksa_sealed_tac_switch]
  S2 = Momentary Switch [package=ksa_sealed_tac_switch]
  S3 = Momentary Switch [package=ksa_sealed_tac_switch]
  S4 = Momentary Switch [package=ksa_sealed_tac_switch]
  S5 = Momentary Switch [package=ksa_sealed_tac_switch]
  R1 = Resistor [tolerance=±5% resistance=10k package=THT]
  R2 = Resistor [tolerance=±5% resistance=10k package=THT]
  R3 = Resistor [tolerance=±5% resistance=4.7k package=THT]
  R4 = Resistor [tolerance=±5% resistance=1k package=THT]
  R5 = Resistor [tolerance=±5% resistance=220 package=THT]
  Part1 = Arduino Nano (Rev3.0)

nets:
  N1: S1.1, S2.1, S3.1, S4.1, S5.1, Part1.A6
  N2: S1.4, R2.Pin_1, R3.Pin_1, R4.Pin_1, R5.Pin_1, Part1.5V
  N3: S2.4, R5.Pin_0
  N4: S3.4, R4.Pin_0
  N5: S4.4, R3.Pin_0
  N6: S5.2, R1.Pin_0
  N7: S5.4, R2.Pin_0
  N8: R1.Pin_1, Part1.GND
  N9: Part1.D2, Part1.D3
